# Fritzing sketch sketch (saved by Fritzing 0.9.2b)
breadboards: 1

parts:
  Part2 = Arduino Uno (Rev3) - ICSP
  Q1 = PNP-Transistor [package="TO92 [THT]"]
  Q2 = PNP-Transistor [package="TO92 [THT]"]
  U3 = G3VM-61E1 [package=g3vm-61e1]
  U4 = G3VM-61E1 [package=g3vm-61e1]
  U5 = G3VM-61E1 [package=g3vm-61e1]
  U6 = G3VM-61E1 [package=g3vm-61e1]
  U7 = G3VM-61E1 [package=g3vm-61e1]
  U8 = G3VM-61E1 [package=g3vm-61e1]
  U9 = G3VM-61E1 [package=g3vm-61e1]
  U10 = G3VM-61E1 [package=g3vm-61e1]
  U11 = POT [package=alps_pot]
  R1 = Photocell (LDR) [package=THT]
  R2 = Resistor [tolerance=±5% resistance=220 package=THT]

nets:
  N1: Part2.A0, U11.S
  N2: Part2.GND, Q1.C, Q2.C, U3.P$3, U4.P$3, U5.P$3, U6.P$3, U7.P$3, U8.P$3, U9.P$3, U10.P$3, U11.E, R2.Pin_0
  N3: Part2.D8, U6.P$2
  N4: Part2.D9_PWM, U5.P$2
  N5: Part2.D10_PWM/SS, U4.P$2
  N6: Part2.D11_PWM/MOSI, U3.P$2
  N7: Part2.D12/MISO, U10.P$2
  N8: Part2.D2, Q1.B
  N9: Part2.D3_PWM, Q2.B
  N10: Part2.D4, R1.pin_0, R2.Pin_1
  N11: Part2.D5_PWM, U9.P$2
  N12: Part2.D6_PWM, U8.P$2
  N13: Part2.D7, U7.P$2
  N14: Part2.VIN, Q1.E, Q2.E, U3.P$1, U4.P$1, U5.P$1, U6.P$1, U7.P$1, U8.P$1, U9.P$1, U10.P$1, U11.A, R1.pin_1

notes:
  PIR
  DÓŁ
  PIR
  GÓRA
  10k
  fotorezystor
  potencjometr 10k
  przekaźniki
  piny 5-13
